# Fritzing sketch beadando (saved by Fritzing 0.9.3b)
breadboards: 1

parts:
  Part1 = Arduino Micro (Rev3)
  S1 = Pushbutton [package="[THT]"]
  LED1 = RGB LED - (4 legs) [package="5 mm [THT]"]
  R1 = Resistor [tolerance=±5% resistance=220 package=THT]
  R3 = Resistor [tolerance=±5% resistance=220 package=THT]
  R4 = Photocell (LDR) [package=THT]
  LED2 = LED - 5mm [color="Red (633nm)" package="5 mm [THT]"]
  R5 = Resistor [tolerance=±5% resistance=10k package=THT]
  R6 = Resistor [tolerance=±5% resistance=220 package=THT]
  R7 = Rotary Potentiometer (Large) [maximum_resistance=100kΩ package=THT]
  R8 = Resistor [tolerance=±5% resistance=10k package=THT]
  R9 = Resistor [tolerance=±5% resistance=220 package=THT]
  ULN2003A_-_Stepper_Driver_Board1 = ULN2003A - Stepper Driver Board [package=board]
  MOTOR1 = 28BYJ-48 Stepper Motor
  LED3 = LED - 5mm [color="Red (633nm)" package="5 mm [THT]"]
  R10 = Resistor [tolerance=±5% resistance=220 package=THT]

nets:
  N1: Part1.GND, LED2.anode, R5.Pin_0, R7.leg2, R8.Pin_1, R10.Pin_1
  N2: Part1.5V, S1.Pin_3, S1.Pin_4, LED1.green_cathode, R4.pin_1, R7.leg1
  N3: S1.Pin_1, S1.Pin_2, R8.Pin_0
  N4: LED1.red_cathode, R1.Pin_1
  N5: LED1.common_anode, R9.Pin_1
  N6: LED1.blue_cathode, R3.Pin_1
  N7: R4.pin_0, R5.Pin_1
  N8: LED2.cathode, R6.Pin_1
  N9: ULN2003A_-_Stepper_Driver_Board1.BLUE, MOTOR1.RED
  N10: ULN2003A_-_Stepper_Driver_Board1.PINK, MOTOR1.ORANGE
  N11: ULN2003A_-_Stepper_Driver_Board1.YELLOW, MOTOR1.YELLOW
  N12: ULN2003A_-_Stepper_Driver_Board1.ORANGE, MOTOR1.PINK
  N13: ULN2003A_-_Stepper_Driver_Board1.RED, MOTOR1.BLUE
  N14: LED3.anode, R10.Pin_0

custom parts:
  ULN2003A - Stepper Driver Board: A common stepper motor driver board based on ULN2003APG darlington array
